// Logisim project ac02.circ as structural Verilog
module memRAMq1 (
  input  [9:0] addr,
  input  in_2,
  input  in_3,
  input  [31:0] data
);

  wire clock_1_out, not_1_out;
  wire [31:0] ram_1_dout;

  Multiplexer multiplexer_1 ();  // open: in0, in1, out, sel
  Shifter #(.width(32)) shifter_1 ();  // open: in, dist, out
  not not_1 (not_1_out, in_2);
  Clock clock_1 (.out(clock_1_out));
  RAM #(.addrWidth(10), .byteenables("byteEnables"), .dataWidth(32)) ram_1 (
    .addr(addr), .we(in_2), .oe(not_1_out), .clk(clock_1_out), .din(data), .dout(ram_1_dout), .be0(in_3));  // open: be3, be2, be1
endmodule
