// Logisim project Lista05.circ as structural Verilog: 15 circuits, main circuit DatapathV1_0
module SystemV1_0 (
);

  wire button_1_out, clock_1_out;
  wire [1:0] datapathv1_0_1_flags;
  wire [2:2] undriven;
  wire [7:0] datapathv1_0_1_memaddr, datapathv1_0_1_memdout, datapathv1_0_1_opcode, ram_1_dout;
  wire [16:0] uInstr;

  Button button_1 (.out(button_1_out));
  Clock clock_1 (.out(clock_1_out));
  ControllerV1_0 controllerv1_0_1 (
    .clk(clock_1_out), .rst(button_1_out), .Opcode(datapathv1_0_1_opcode), .Flags(datapathv1_0_1_flags),
    .uInstr(uInstr));
  DatapathV1_0 datapathv1_0_1 (
    .rst(button_1_out), .clk(clock_1_out), .MemDin(ram_1_dout), .uInstr(uInstr),
    .MemDout(datapathv1_0_1_memdout), .MemAddr(datapathv1_0_1_memaddr), .Opcode(datapathv1_0_1_opcode),
    .Flags(datapathv1_0_1_flags));
  RAM #(.asyncread("true"), .\type ("nonvolatile")) ram_1 (
    .addr(datapathv1_0_1_memaddr), .we(uInstr[15]), .oe(uInstr[16]), .clk(clock_1_out),
    .din(datapathv1_0_1_memdout), .dout(ram_1_dout));
  LED led_1 (.in(undriven[2]));
  LED ALUop (.in(uInstr[1]));
  LED led_2 (.in(uInstr[0]));
  LED MARwr (.in(uInstr[2]));
  LED ACCcl (.in(uInstr[4]));
  LED ACCrd (.in(uInstr[6]));
  LED ACCwr (.in(uInstr[8]));
  LED PCrd (.in(uInstr[9]));
  LED PCwr (.in(uInstr[10]));
  LED MDRrd (.in(uInstr[11]));
  LED MDRwr (.in(uInstr[12]));
  LED IRwr (.in(uInstr[13]));
  LED FLGwr (.in(uInstr[14]));
  LED MEMwr (.in(uInstr[15]));
  LED MEMrd (.in(uInstr[16]));
  // Pins of 2 and 3 bits meet at {undriven[2], uInstr[1:0]}
  // Pins of 1 and 2 bits meet at uInstr[3:2]
  // Pins of 1 and 2 bits meet at uInstr[5:4]
  // Pins of 1 and 2 bits meet at uInstr[7:6]
endmodule

module DatapathV1_0 (
  input  [16:0] uInstr,
  input  [7:0] MemDin,
  input  rst,
  input  clk,
  output [7:0] MemDout,
  output [7:0] MemAddr,
  output [7:0] Opcode,
  output [1:0] Flags
);

  wire ACCcl, ACCrd, ACCwr, MARwr, or_1_out;
  wire [1:0] alu_1_flagsout;
  wire [2:0] ALUop;
  wire [7:0] A_q, ACC_q, alu_1_cbus, controlled_buffer_1_out, MDR_q, multiplexer_1_out, PC_q;

  Multiplexer #(.width(8)) multiplexer_1 (
    .in0(controlled_buffer_1_out), .in1(MemDin), .out(multiplexer_1_out), .sel(uInstr[16]));
  Register MDR (.D(multiplexer_1_out), .en(uInstr[12]), .clk(clk), .Q(MDR_q), .clr(rst));
  Register IR (.D(MemDin), .en(uInstr[13]), .clk(clk), .Q(Opcode), .clr(rst));
  assign controlled_buffer_1_out = uInstr[11] ? MDR_q : 8'bz;  // Controlled_Buffer controlled_buffer_1
  assign MemDout = uInstr[15] ? MDR_q : 8'bz;  // Controlled_Buffer controlled_buffer_2
  Register PC (.D(controlled_buffer_1_out), .en(uInstr[10]), .clk(clk), .Q(PC_q), .clr(rst));
  assign controlled_buffer_1_out = uInstr[9] ? PC_q : 8'bz;  // Controlled_Buffer controlled_buffer_3
  Register A (.D(controlled_buffer_1_out), .en(uInstr[8]), .clk(clk), .Q(A_q), .clr(rst));
  assign controlled_buffer_1_out = uInstr[7] ? A_q : 8'bz;  // Controlled_Buffer controlled_buffer_4
  LED Z (.in(alu_1_flagsout[1]));
  Register #(.width(2)) FLG (.D(alu_1_flagsout), .en(uInstr[14]), .clk(clk), .Q(Flags), .clr(rst));
  ALU alu_1 (.Bbus(controlled_buffer_1_out), .ALUop(ALUop), .Abus(ACC_q), .FLAGSout(alu_1_flagsout), .Cbus(alu_1_cbus));
  LED N (.in(alu_1_flagsout[0]));
  assign controlled_buffer_1_out = ACCrd ? ACC_q : 8'bz;  // Controlled_Buffer controlled_buffer_5
  Register ACC (.D(alu_1_cbus), .en(ACCwr), .clk(clk), .Q(ACC_q), .clr(or_1_out));
  or or_1 (or_1_out, rst, ACCcl);
  Register MAR (.D(controlled_buffer_1_out), .en(MARwr), .clk(clk), .Q(MemAddr), .clr(rst));

  // Other names for the same wires on the sheet: Ard = uInstr[7]; Awr = uInstr[8]; PCrd = uInstr[9];
  //   PCwr = uInstr[10]; MDRrd = uInstr[11]; MDRwr = uInstr[12]; IRwr = uInstr[13]; FLGwr = uInstr[14];
  //   MEMwr = uInstr[15]; MEMrd = uInstr[16]
endmodule

module ControllerV1_0 (
  input  [7:0] Opcode,
  input  clk,
  input  rst,
  input  [1:0] Flags,
  output [16:0] uInstr
);

  wire Exec, multiplexer_2_out;
  wire [1:0] uJump;
  wire [2:0] Action;
  wire [7:0] adder_1_out, multiplexer_1_out, Translate_out, uAddr_q;
  wire [19:3] rom_1_data;

  PLA #(.in_width(8), .out_width(8), .\table ("00000000 00000010 # NOP")) Translate (.in(Opcode), .out(Translate_out));
  Multiplexer #(.select(2), .width(8)) multiplexer_1 (
    .in0({8{1'b0}}), .in1(adder_1_out), .in2(Translate_out), .out(multiplexer_1_out), .sel(uJump));  // open: in3
  Multiplexer #(.select(2)) multiplexer_2 (
    .in0(Flags[0]), .in1(Flags[1]), .out(multiplexer_2_out), .sel(Action[1:0]));  // open: in2, in3
  Register #(.trigger("falling")) uAddr (.D(multiplexer_1_out), .en(1'b1), .clk(clk), .Q(uAddr_q), .clr(rst));
  or or_1 (Exec, multiplexer_2_out, ~Action[2]);  // OR_Gate
  Multiplexer #(.width(2)) multiplexer_3 (.in0(Action[1:0]), .in1(2'b01), .out(uJump), .sel(Action[2]));
  Adder adder_1 (.a(8'h1), .b(uAddr_q), .out(adder_1_out));  // open: cin, cout
  ROM #(.dataWidth(20)) rom_1 (.addr(uAddr_q), .data({rom_1_data, Action}));
  assign uInstr = Exec ? rom_1_data : 17'bz;  // Controlled_Buffer controlled_buffer_1
  Pull_Resistor pull_resistor_1 (.node(uInstr));

  // Notes on the sheet:
  //   contents of rom_1 (hex, n*v repeats v):
  //   3ff81 2a 4
  //   100  FETCH
  //   101  NEXT
  //   110  DISPATCH
  //   000  CondN
  //   001  CondZ
endmodule

module ALU (
  input  [7:0] Abus,
  input  [7:0] Bbus,
  input  [2:0] ALUop,
  output [7:0] Cbus,
  output [1:0] FLAGSout
);

  wire adder8_1_carry, C, V;
  wire [7:0] adder8_1_result, and_1_out, multiplexer_1_out, not_1_out, or_1_out, shifter_1_out,
       shifter_2_out, shifter_3_out;

  Multiplexer #(.width(8)) multiplexer_1 (.in0(Abus), .in1({8{1'b0}}), .out(multiplexer_1_out), .sel(ALUop[2]));
  assign and_1_out = Abus & Bbus;  // AND_Gate and_1, 8 bits wide
  assign or_1_out = Abus | Bbus;  // OR_Gate or_1, 8 bits wide
  assign not_1_out = ~Bbus;  // NOT_Gate not_1, 8 bits wide
  Adder8 adder8_1 (
    .Cin(ALUop[2]), .A(multiplexer_1_out), .B(Bbus), .Result(adder8_1_result), .oVerflow(V),
    .Carry(adder8_1_carry));
  Shifter #(.shift("lr")) shifter_1 (.in(Bbus), .\dist (3'b001), .out(shifter_1_out));
  Shifter shifter_2 (.in(Bbus), .\dist (3'b001), .out(shifter_2_out));
  Shifter #(.shift("ar")) shifter_3 (.in(Bbus), .\dist (3'b001), .out(shifter_3_out));
  Multiplexer #(.select(3)) multiplexer_2 (
    .in0(adder8_1_carry), .in1(1'b0), .in2(1'b0), .in3(1'b0), .in4(adder8_1_carry), .in5(Bbus[0]),
    .in6(Bbus[7]), .in7(Bbus[0]), .out(C), .sel(ALUop));
  Multiplexer #(.select(3), .width(8)) multiplexer_3 (
    .in0(adder8_1_result), .in1(and_1_out), .in2(or_1_out), .in3(not_1_out), .in4(adder8_1_result),
    .in5(shifter_1_out), .in6(shifter_2_out), .in7(shifter_3_out), .out(Cbus), .sel(ALUop));
  nor nor_1 (FLAGSout[1], Cbus[0], Cbus[1], Cbus[2], Cbus[3], Cbus[4], Cbus[5], Cbus[6], Cbus[7]);

  assign FLAGSout[0] = Cbus[7];

  // Other names for the same wires on the sheet: inc = ALUop[2]; N = Cbus[7]; Z = FLAGSout[1]

  // Notes on the sheet:
  //   ALUop Função Observação
  //    000   ADD   C = A + B
  //    001   AND   C = A and B
  //    010   OR    C = A or B
  //    011   NOT   C = not B
  //    100   INC   C = B + 1
  //    101   SRL   C = B >> 1
  //    110   SLL   C = B << 1
  //    111   SRA   C = B >> 1 preserva b7
endmodule

module Adder8 (
  input  Cin,
  input  [7:0] A,
  input  [7:0] B,
  output [7:0] Result,
  output oVerflow,
  output Carry
);

  wire adder_1_cout;

  Adder #(.width(7)) adder_1 (.a(A[6:0]), .b(B[6:0]), .out(Result[6:0]), .cin(Cin), .cout(adder_1_cout));
  Adder #(.width(1)) adder_2 (.a(A[7]), .b(B[7]), .out(Result[7]), .cin(adder_1_cout), .cout(Carry));
  xor xor_1 (oVerflow, adder_1_cout, Carry);
endmodule

module Q2_ALU (
  input  [7:0] Abus,
  input  [7:0] Bbus,
  input  [2:0] ALUop,
  output [7:0] Cbus,
  output [2:0] FLAGSout
);

  wire adder8_1_carry, V;
  wire [7:0] adder8_1_result, and_1_out, multiplexer_1_out, not_1_out, or_1_out, shifter_1_out,
       shifter_2_out, shifter_3_out;

  Multiplexer #(.width(8)) multiplexer_1 (.in0(Abus), .in1({8{1'b0}}), .out(multiplexer_1_out), .sel(ALUop[2]));
  assign and_1_out = Abus & Bbus;  // AND_Gate and_1, 8 bits wide
  assign or_1_out = Abus | Bbus;  // OR_Gate or_1, 8 bits wide
  assign not_1_out = ~Bbus;  // NOT_Gate not_1, 8 bits wide
  Adder8 adder8_1 (
    .Cin(ALUop[2]), .A(multiplexer_1_out), .B(Bbus), .Result(adder8_1_result), .oVerflow(V),
    .Carry(adder8_1_carry));
  Shifter #(.shift("lr")) shifter_1 (.in(Bbus), .\dist (3'b001), .out(shifter_1_out));
  Shifter shifter_2 (.in(Bbus), .\dist (3'b001), .out(shifter_2_out));
  Shifter #(.shift("ar")) shifter_3 (.in(Bbus), .\dist (3'b001), .out(shifter_3_out));
  Multiplexer #(.select(3)) multiplexer_2 (
    .in0(adder8_1_carry), .in1(1'b0), .in2(1'b0), .in3(1'b0), .in4(adder8_1_carry), .in5(Bbus[0]),
    .in6(Bbus[7]), .in7(Bbus[0]), .out(FLAGSout[2]), .sel(ALUop));
  Multiplexer #(.select(3), .width(8)) multiplexer_3 (
    .in0(adder8_1_result), .in1(and_1_out), .in2(or_1_out), .in3(not_1_out), .in4(adder8_1_result),
    .in5(shifter_1_out), .in6(shifter_2_out), .in7(shifter_3_out), .out(Cbus), .sel(ALUop));
  nor nor_1 (FLAGSout[1], Cbus[0], Cbus[1], Cbus[2], Cbus[3], Cbus[4], Cbus[5], Cbus[6], Cbus[7]);

  assign FLAGSout[0] = Cbus[7];

  // Other names for the same wires on the sheet: inc = ALUop[2]; N = Cbus[7]; Z = FLAGSout[1]; C = FLAGSout[2]

  // Notes on the sheet:
  //   ALUop Função Observação
  //    000   ADD   C = A + B
  //    001   AND   C = A and B
  //    010   OR    C = A or B
  //    011   NOT   C = not B
  //    100   INC   C = B + 1
  //    101   SRL   C = B >> 1
  //    110   SLL   C = B << 1
  //    111   SRA   C = B >> 1 preserva b7
endmodule

module Q2_Datapath (
  input  [14:0] uInstr,
  input  [7:0] MemDin,
  input  rst,
  input  clk,
  output [7:0] MemDout,
  output [7:0] MemAddr,
  output [7:0] Opcode,
  output [2:0] Flags
);

  wire Ard, Awr, or_1_out;
  wire [2:0] q2_alu_1_flagsout;
  wire [7:0] A_q, ACC_q, controlled_buffer_1_out, MDR_q, multiplexer_1_out, PC_q, q2_alu_1_cbus;

  Multiplexer #(.width(8)) multiplexer_1 (
    .in0(controlled_buffer_1_out), .in1(MemDin), .out(multiplexer_1_out), .sel(uInstr[14]));
  Register MDR (.D(multiplexer_1_out), .en(uInstr[10]), .clk(clk), .Q(MDR_q), .clr(rst));
  Register IR (.D(MemDin), .en(uInstr[11]), .clk(clk), .Q(Opcode), .clr(rst));
  assign controlled_buffer_1_out = uInstr[9] ? MDR_q : 8'bz;  // Controlled_Buffer controlled_buffer_1
  assign MemDout = uInstr[13] ? MDR_q : 8'bz;  // Controlled_Buffer controlled_buffer_2
  Register PC (.D(controlled_buffer_1_out), .en(uInstr[8]), .clk(clk), .Q(PC_q), .clr(rst));
  assign controlled_buffer_1_out = uInstr[7] ? PC_q : 8'bz;  // Controlled_Buffer controlled_buffer_3
  Register A (.D(controlled_buffer_1_out), .en(Awr), .clk(clk), .Q(A_q), .clr(rst));
  assign controlled_buffer_1_out = Ard ? A_q : 8'bz;  // Controlled_Buffer controlled_buffer_4
  LED C (.in(q2_alu_1_flagsout[2]));
  Register #(.width(3)) FLG (.D(q2_alu_1_flagsout), .en(uInstr[12]), .clk(clk), .Q(Flags), .clr(rst));
  Q2_ALU q2_alu_1 (
    .Bbus(controlled_buffer_1_out), .ALUop(uInstr[2:0]), .Abus(ACC_q), .FLAGSout(q2_alu_1_flagsout),
    .Cbus(q2_alu_1_cbus));
  LED Z (.in(q2_alu_1_flagsout[1]));
  LED N (.in(q2_alu_1_flagsout[0]));
  assign controlled_buffer_1_out = uInstr[5] ? ACC_q : 8'bz;  // Controlled_Buffer controlled_buffer_5
  Register ACC (.D(q2_alu_1_cbus), .en(uInstr[6]), .clk(clk), .Q(ACC_q), .clr(or_1_out));
  or or_1 (or_1_out, rst, uInstr[4]);
  Register MAR (.D(controlled_buffer_1_out), .en(uInstr[3]), .clk(clk), .Q(MemAddr), .clr(rst));

  // Other names for the same wires on the sheet: ALUop[2:0] = uInstr[2:0]; MARwr = uInstr[3]; ACCcl = uInstr[4];
  //   ACCrd = uInstr[5]; ACCwr = uInstr[6]; PCrd = uInstr[7]; PCwr = uInstr[8]; MDRrd = uInstr[9]; MDRwr = uInstr[10];
  //   IRwr = uInstr[11]; FLGwr = uInstr[12]; MEMwr = uInstr[13]; MEMrd = uInstr[14]
endmodule

module Q2_Controller (
  input  [7:0] Opcode,
  input  clk,
  input  rst,
  input  [2:0] Flags,
  output [16:0] uInstr
);

  wire Exec, multiplexer_2_out;
  wire [1:0] uJump;
  wire [2:0] Action;
  wire [7:0] adder_1_out, multiplexer_1_out, Translate_out, uAddr_q;
  wire [19:3] rom_1_data;

  PLA #(.in_width(8), .out_width(8), .\table ("00000000 00000010 # NOP")) Translate (.in(Opcode), .out(Translate_out));
  Multiplexer #(.select(2), .width(8)) multiplexer_1 (
    .in0({8{1'b0}}), .in1(adder_1_out), .in2(Translate_out), .out(multiplexer_1_out), .sel(uJump));  // open: in3
  Multiplexer #(.select(2)) multiplexer_2 (
    .in0(Flags[0]), .in1(Flags[1]), .in2(Flags[2]), .out(multiplexer_2_out), .sel(Action[1:0]));  // open: in3
  Register #(.trigger("falling")) uAddr (.D(multiplexer_1_out), .en(1'b1), .clk(clk), .Q(uAddr_q), .clr(rst));
  or or_1 (Exec, multiplexer_2_out, Action[2]);
  Multiplexer #(.width(2)) multiplexer_3 (.in0(2'b01), .in1(Action[1:0]), .out(uJump), .sel(Action[2]));
  Adder adder_1 (.a(8'h1), .b(uAddr_q), .out(adder_1_out));  // open: cin, cout
  ROM #(.dataWidth(20)) rom_1 (.addr(uAddr_q), .data({rom_1_data, Action}));
  Pull_Resistor pull_resistor_1 (.node(uInstr));
  assign uInstr = Exec ? rom_1_data : 17'bz;  // Controlled_Buffer controlled_buffer_1

  // Notes on the sheet:
  //   contents of rom_1 (hex, n*v repeats v):
  //   3ff81 2a 4
  //   000  CondN
  //   001  CondZ
  //   010  CondC
  //   100  FETCH
  //   101  NEXT
  //   110  DISPATCH
endmodule

module Q3_Controller (
  input  [7:0] Opcode,
  input  clk,
  input  rst,
  input  [2:0] Flags,
  output [16:0] uInstr
);

  wire Exec, multiplexer_1_out, xor_1_out;
  wire [1:0] uJump;
  wire [3:0] Action;
  wire [7:0] adder_1_out, multiplexer_2_out, Translate_out, uAddr_q;
  wire [20:4] rom_1_data;

  PLA #(.in_width(8), .out_width(8), .\table ("00000000 00000010 # NOP")) Translate (.in(Opcode), .out(Translate_out));
  Multiplexer #(.select(2)) multiplexer_1 (
    .in0(Flags[0]), .in1(Flags[1]), .in2(Flags[2]), .out(multiplexer_1_out), .sel(Action[1:0]));  // open: in3
  Multiplexer #(.select(2), .width(8)) multiplexer_2 (
    .in0({8{1'b0}}), .in1(adder_1_out), .in2(Translate_out), .out(multiplexer_2_out), .sel(uJump));  // open: in3
  xor xor_1 (xor_1_out, multiplexer_1_out, Action[2]);
  or or_1 (Exec, xor_1_out, Action[3]);
  Multiplexer #(.width(2)) multiplexer_3 (.in0(2'b01), .in1(Action[1:0]), .out(uJump), .sel(Action[3]));
  Register #(.trigger("falling")) uAddr (.D(multiplexer_2_out), .en(1'b1), .clk(clk), .Q(uAddr_q), .clr(rst));
  Adder adder_1 (.a(8'h1), .b(uAddr_q), .out(adder_1_out));  // open: cin, cout
  ROM #(.dataWidth(21)) rom_1 (.addr(uAddr_q), .data({rom_1_data, Action}));
  Pull_Resistor pull_resistor_1 (.node(uInstr));
  assign uInstr = Exec ? rom_1_data : 17'bz;  // Controlled_Buffer controlled_buffer_1

  // Notes on the sheet:
  //   contents of rom_1 (hex, n*v repeats v):
  //   3ff81 2a 4
  //   0000  CondN
  //   0001  CondZ
  //   0010  CondC
  //   0100  CondNN
  //   0101  CondNZ
  //   0110  CondNC
  //   1000  FETCH
  //   1001  NEXT
  //   1010  DISPATCH
endmodule

module Q4_Datapath (
  input  [18:0] uInstr,
  input  [7:0] MemDin,
  input  rst,
  input  clk,
  output [7:0] MemDout,
  output [7:0] MemAddr,
  output [7:0] Opcode,
  output [2:0] Flags
);

  wire or_1_out;
  wire [2:0] q2_alu_1_flagsout;
  wire [7:0] A_q, ACC_q, controlled_buffer_1_out, MDR_q, multiplexer_1_out, PC_q, q2_alu_1_cbus, SP_q;

  Multiplexer #(.width(8)) multiplexer_1 (
    .in0(controlled_buffer_1_out), .in1(MemDin), .out(multiplexer_1_out), .sel(uInstr[18]));
  Register MDR (.D(multiplexer_1_out), .en(uInstr[14]), .clk(clk), .Q(MDR_q), .clr(rst));
  Register IR (.D(MemDin), .en(uInstr[15]), .clk(clk), .Q(Opcode), .clr(rst));
  assign controlled_buffer_1_out = uInstr[13] ? MDR_q : 8'bz;  // Controlled_Buffer controlled_buffer_1
  assign MemDout = uInstr[17] ? MDR_q : 8'bz;  // Controlled_Buffer controlled_buffer_2
  Register PC (.D(controlled_buffer_1_out), .en(uInstr[12]), .clk(clk), .Q(PC_q), .clr(rst));
  assign controlled_buffer_1_out = uInstr[11] ? PC_q : 8'bz;  // Controlled_Buffer controlled_buffer_3
  Register SP (.D(controlled_buffer_1_out), .en(uInstr[10]), .clk(clk), .Q(SP_q), .clr(rst));
  assign controlled_buffer_1_out = uInstr[9] ? SP_q : 8'bz;  // Controlled_Buffer controlled_buffer_4
  Register A (.D(controlled_buffer_1_out), .en(uInstr[8]), .clk(clk), .Q(A_q), .clr(rst));
  assign controlled_buffer_1_out = uInstr[7] ? A_q : 8'bz;  // Controlled_Buffer controlled_buffer_5
  Q2_ALU q2_alu_1 (
    .Bbus(controlled_buffer_1_out), .ALUop(uInstr[2:0]), .Abus(ACC_q), .FLAGSout(q2_alu_1_flagsout),
    .Cbus(q2_alu_1_cbus));
  LED C (.in(q2_alu_1_flagsout[2]));
  LED Z (.in(q2_alu_1_flagsout[1]));
  LED N (.in(q2_alu_1_flagsout[0]));
  Register #(.width(3)) FLG (.D(q2_alu_1_flagsout), .en(uInstr[16]), .clk(clk), .Q(Flags), .clr(rst));
  Register ACC (.D(q2_alu_1_cbus), .en(uInstr[6]), .clk(clk), .Q(ACC_q), .clr(or_1_out));
  or or_1 (or_1_out, rst, uInstr[4]);
  assign controlled_buffer_1_out = uInstr[5] ? ACC_q : 8'bz;  // Controlled_Buffer controlled_buffer_6
  Register MAR (.D(controlled_buffer_1_out), .en(uInstr[3]), .clk(clk), .Q(MemAddr), .clr(rst));

  // Other names for the same wires on the sheet: ALUop[2:0] = uInstr[2:0]; MARwr = uInstr[3]; ACCcl = uInstr[4];
  //   ACCrd = uInstr[5]; ACCwr = uInstr[6]; Ard = uInstr[7]; Awr = uInstr[8]; SPrd = uInstr[9]; SPwr = uInstr[10];
  //   PCrd = uInstr[11]; PCwr = uInstr[12]; MDRrd = uInstr[13]; MDRwr = uInstr[14]; IRwr = uInstr[15];
  //   FLGwr = uInstr[16]; MEMwr = uInstr[17]; MEMrd = uInstr[18]
endmodule

module Q4_Controller (
  input  [7:0] Opcode,
  input  clk,
  input  rst,
  input  [2:0] Flags,
  output [18:0] uInstr
);

  wire Exec, multiplexer_1_out, xor_1_out;
  wire [1:0] uJump;
  wire [3:0] Action;
  wire [7:0] adder_1_out, multiplexer_2_out, Translate_out, uAddr_q;
  wire [22:4] rom_1_data;

  PLA #(.in_width(8), .out_width(8), .\table ("00000000 00000010 # NOP")) Translate (.in(Opcode), .out(Translate_out));
  Multiplexer #(.select(2)) multiplexer_1 (
    .in0(Flags[0]), .in1(Flags[1]), .in2(Flags[2]), .out(multiplexer_1_out), .sel(Action[1:0]));  // open: in3
  Multiplexer #(.select(2), .width(8)) multiplexer_2 (
    .in0({8{1'b0}}), .in1(adder_1_out), .in2(Translate_out), .out(multiplexer_2_out), .sel(uJump));  // open: in3
  xor xor_1 (xor_1_out, multiplexer_1_out, Action[2]);
  or or_1 (Exec, xor_1_out, Action[3]);
  Multiplexer #(.width(2)) multiplexer_3 (.in0(2'b01), .in1(Action[1:0]), .out(uJump), .sel(Action[3]));
  Register #(.trigger("falling")) uAddr (.D(multiplexer_2_out), .en(1'b1), .clk(clk), .Q(uAddr_q), .clr(rst));
  Adder adder_1 (.a(8'h1), .b(uAddr_q), .out(adder_1_out));  // open: cin, cout
  ROM #(.dataWidth(23)) rom_1 (.addr(uAddr_q), .data({rom_1_data, Action}));
  Pull_Resistor pull_resistor_1 (.node(uInstr));
  assign uInstr = Exec ? rom_1_data : 19'bz;  // Controlled_Buffer controlled_buffer_1

  // Notes on the sheet:
  //   contents of rom_1 (hex, n*v repeats v):
  //   3ff81 2a 4
  //   0000  CondN
  //   0001  CondZ
  //   0010  CondC
  //   0100  CondNN
  //   0101  CondNZ
  //   0110  CondNC
  //   1000  FETCH
  //   1001  NEXT
  //   1010  DISPATCH
endmodule

module Q8_Datapath (
  input  [24:0] uInstr,
  input  [7:0] MemDin,
  input  rst,
  input  clk,
  output [7:0] MemDout,
  output [15:0] MemAddr,
  output [7:0] Opcode,
  output [3:0] Flags
);

  wire Hrd, Hwr, Lrd, Lwr, or_1_out, PCHrd, PCHwr, PCLrd, PCLwr, SPHrd, SPHwr, SPLrd, SPLwr;
  wire [2:0] q2_alu_1_flagsout;
  wire [7:0] A_q, ACC_q, controlled_buffer_1_out, MDR_q, multiplexer_1_out, PCH_q, PCL_q, q2_alu_1_cbus,
       register_1_q, register_2_q, SPH_q, SPL_q;

  Multiplexer #(.width(8)) multiplexer_1 (
    .in0(controlled_buffer_1_out), .in1(MemDin), .out(multiplexer_1_out), .sel(uInstr[24]));
  Register MDR (.D(multiplexer_1_out), .en(uInstr[19]), .clk(clk), .Q(MDR_q), .clr(rst));
  Register IR (.D(MemDin), .en(uInstr[20]), .clk(clk), .Q(Opcode), .clr(rst));
  assign controlled_buffer_1_out = uInstr[18] ? MDR_q : 8'bz;  // Controlled_Buffer controlled_buffer_1
  assign MemDout = uInstr[23] ? MDR_q : 8'bz;  // Controlled_Buffer controlled_buffer_2
  Register register_1 (.D(controlled_buffer_1_out), .en(Hwr), .clk(clk), .Q(register_1_q), .clr(rst));
  assign controlled_buffer_1_out = Hrd ? register_1_q : 8'bz;  // Controlled_Buffer controlled_buffer_3
  Register register_2 (.D(controlled_buffer_1_out), .en(Lwr), .clk(clk), .Q(register_2_q), .clr(rst));
  assign controlled_buffer_1_out = Lrd ? register_2_q : 8'bz;  // Controlled_Buffer controlled_buffer_4
  Register PCH (.D(controlled_buffer_1_out), .en(PCHwr), .clk(clk), .Q(PCH_q), .clr(rst));
  assign controlled_buffer_1_out = PCHrd ? PCH_q : 8'bz;  // Controlled_Buffer controlled_buffer_5
  Register PCL (.D(controlled_buffer_1_out), .en(PCLwr), .clk(clk), .Q(PCL_q), .clr(rst));
  assign controlled_buffer_1_out = PCLrd ? PCL_q : 8'bz;  // Controlled_Buffer controlled_buffer_6
  Register SPH (.D(controlled_buffer_1_out), .en(SPHwr), .clk(clk), .Q(SPH_q), .clr(rst));
  assign controlled_buffer_1_out = SPHrd ? SPH_q : 8'bz;  // Controlled_Buffer controlled_buffer_7
  Register SPL (.D(controlled_buffer_1_out), .en(SPLwr), .clk(clk), .Q(SPL_q), .clr(rst));
  assign controlled_buffer_1_out = SPLrd ? SPL_q : 8'bz;  // Controlled_Buffer controlled_buffer_8
  Register A (.D(controlled_buffer_1_out), .en(uInstr[9]), .clk(clk), .Q(A_q), .clr(rst));
  assign controlled_buffer_1_out = uInstr[8] ? A_q : 8'bz;  // Controlled_Buffer controlled_buffer_9
  Q2_ALU q2_alu_1 (
    .Bbus(controlled_buffer_1_out), .ALUop(uInstr[2:0]), .Abus(ACC_q), .FLAGSout(q2_alu_1_flagsout),
    .Cbus(q2_alu_1_cbus));
  LED C (.in(q2_alu_1_flagsout[2]));
  LED Z (.in(q2_alu_1_flagsout[1]));
  LED N (.in(q2_alu_1_flagsout[0]));
  Register #(.width(1)) SFLG (.D(q2_alu_1_flagsout[2]), .en(uInstr[21]), .clk(clk), .Q(Flags[3]), .clr(rst));
  Register ACC (.D(q2_alu_1_cbus), .en(uInstr[7]), .clk(clk), .Q(ACC_q), .clr(or_1_out));
  or or_1 (or_1_out, rst, uInstr[5]);
  Register #(.width(3)) FLG (.D(q2_alu_1_flagsout), .en(uInstr[22]), .clk(clk), .Q(Flags[2:0]), .clr(rst));
  assign controlled_buffer_1_out = uInstr[6] ? ACC_q : 8'bz;  // Controlled_Buffer controlled_buffer_10
  Register MARH (.D(controlled_buffer_1_out), .en(uInstr[4]), .clk(clk), .Q(MemAddr[15:8]), .clr(rst));
  Register MARL (.D(controlled_buffer_1_out), .en(uInstr[3]), .clk(clk), .Q(MemAddr[7:0]), .clr(rst));

  assign {uInstr[15:14], uInstr[11:10]} = {uInstr[17:16], uInstr[13:12]};

  // Other names for the same wires on the sheet: ALUop[2:0] = uInstr[2:0]; MARLwr = uInstr[3]; MARHwr = uInstr[4];
  //   ACCcl = uInstr[5]; ACCrd = uInstr[6]; ACCwr = uInstr[7]; Ard = uInstr[8]; Awr = uInstr[9]; SPrd = uInstr[12];
  //   SPwr = uInstr[13]; PCrd = uInstr[16]; PCwr = uInstr[17]; MDRrd = uInstr[18]; MDRwr = uInstr[19];
  //   IRwr = uInstr[20]; SFLGwr = uInstr[21]; FLGwr = uInstr[22]; MEMwr = uInstr[23]; MEMrd = uInstr[24]

  // Notes on the sheet:
  //   OBS: O bit 3 armazena SC
  //   (System Carry) que é
  //   escrito com SFLGwr
endmodule

module Q8_Controller (
  input  [7:0] Opcode,
  input  clk,
  input  rst,
  input  [3:0] Flags,
  output [20:0] uInstr
);

  wire Exec, multiplexer_1_out, xor_1_out;
  wire [1:0] uJump;
  wire [3:0] Action;
  wire [7:0] adder_1_out, multiplexer_2_out, Translate_out, uAddr_q;
  wire [24:4] rom_1_data;

  PLA #(.in_width(8), .out_width(8), .\table ("00000000 00000010 # NOP")) Translate (.in(Opcode), .out(Translate_out));
  Multiplexer #(.select(2)) multiplexer_1 (
    .in0(Flags[0]), .in1(Flags[1]), .in2(Flags[2]), .in3(Flags[3]), .out(multiplexer_1_out), .sel(Action[1:0]));
  Multiplexer #(.select(2), .width(8)) multiplexer_2 (
    .in0({8{1'b0}}), .in1(adder_1_out), .in2(Translate_out), .out(multiplexer_2_out), .sel(uJump));  // open: in3
  xor xor_1 (xor_1_out, multiplexer_1_out, Action[2]);
  Register #(.trigger("falling")) uAddr (.D(multiplexer_2_out), .en(1'b1), .clk(clk), .Q(uAddr_q), .clr(rst));
  or or_1 (Exec, xor_1_out, Action[3]);
  Multiplexer #(.width(2)) multiplexer_3 (.in0(2'b01), .in1(Action[1:0]), .out(uJump), .sel(Action[3]));
  Adder adder_1 (.a(8'h1), .b(uAddr_q), .out(adder_1_out));  // open: cin, cout
  ROM #(.dataWidth(25)) rom_1 (.addr(uAddr_q), .data({rom_1_data, Action}));
  assign uInstr = Exec ? rom_1_data : 21'bz;  // Controlled_Buffer controlled_buffer_1
  Pull_Resistor pull_resistor_1 (.node(uInstr));

  // Notes on the sheet:
  //   contents of rom_1 (hex, n*v repeats v):
  //   3ff81 2a 4
  //   0000  CondN
  //   0001  CondZ
  //   0010  CondC
  //   0010  CondSC
  //   0100  CondNN
  //   0101  CondNZ
  //   0110  CondNC
  //   0010  CondNSC
  //   1000  FETCH
  //   1001  NEXT
  //   1010  DISPATCH
endmodule

module Q9_Datapath (
  input  [20:0] uInstr,
  input  [7:0] MemDin,
  input  rst,
  input  clk,
  output [7:0] MemDout,
  output [7:0] IMemAddr,
  output [7:0] SMemAddr,
  output [7:0] DMemAddr,
  output [7:0] Opcode,
  output [2:0] Flags
);

  wire or_1_out;
  wire [2:0] q2_alu_1_flagsout;
  wire [7:0] A_q, ACC_q, controlled_buffer_1_out, MDR_q, multiplexer_1_out, q2_alu_1_cbus;

  Multiplexer #(.width(8)) multiplexer_1 (
    .in0(controlled_buffer_1_out), .in1(MemDin), .out(multiplexer_1_out), .sel(uInstr[20]));
  Register MDR (.D(multiplexer_1_out), .en(uInstr[14]), .clk(clk), .Q(MDR_q), .clr(rst));
  Register IR (.D(MemDin), .en(uInstr[15]), .clk(clk), .Q(Opcode), .clr(rst));
  assign controlled_buffer_1_out = uInstr[13] ? MDR_q : 8'bz;  // Controlled_Buffer controlled_buffer_1
  assign MemDout = uInstr[19] ? MDR_q : 8'bz;  // Controlled_Buffer controlled_buffer_2
  Register PC (.D(controlled_buffer_1_out), .en(uInstr[12]), .clk(clk), .Q(IMemAddr), .clr(rst));
  assign controlled_buffer_1_out = uInstr[11] ? IMemAddr : 8'bz;  // Controlled_Buffer controlled_buffer_3
  Register SP (.D(controlled_buffer_1_out), .en(uInstr[10]), .clk(clk), .Q(SMemAddr), .clr(rst));
  assign controlled_buffer_1_out = uInstr[9] ? SMemAddr : 8'bz;  // Controlled_Buffer controlled_buffer_4
  Register A (.D(controlled_buffer_1_out), .en(uInstr[8]), .clk(clk), .Q(A_q), .clr(rst));
  assign controlled_buffer_1_out = uInstr[7] ? A_q : 8'bz;  // Controlled_Buffer controlled_buffer_5
  Q2_ALU q2_alu_1 (
    .Bbus(controlled_buffer_1_out), .ALUop(uInstr[2:0]), .Abus(ACC_q), .FLAGSout(q2_alu_1_flagsout),
    .Cbus(q2_alu_1_cbus));
  LED C (.in(q2_alu_1_flagsout[2]));
  LED Z (.in(q2_alu_1_flagsout[1]));
  LED N (.in(q2_alu_1_flagsout[0]));
  Register #(.width(3)) FLG (.D(q2_alu_1_flagsout), .en(uInstr[16]), .clk(clk), .Q(Flags), .clr(rst));
  Register ACC (.D(q2_alu_1_cbus), .en(uInstr[6]), .clk(clk), .Q(ACC_q), .clr(or_1_out));
  or or_1 (or_1_out, rst, uInstr[4]);
  assign controlled_buffer_1_out = uInstr[5] ? ACC_q : 8'bz;  // Controlled_Buffer controlled_buffer_6
  Register MAR (.D(controlled_buffer_1_out), .en(uInstr[3]), .clk(clk), .Q(DMemAddr), .clr(rst));

  // Other names for the same wires on the sheet: ALUop[2:0] = uInstr[2:0]; MARwr = uInstr[3]; ACCcl = uInstr[4];
  //   ACCrd = uInstr[5]; ACCwr = uInstr[6]; Ard = uInstr[7]; Awr = uInstr[8]; SPrd = uInstr[9]; SPwr = uInstr[10];
  //   PCrd = uInstr[11]; PCwr = uInstr[12]; MDRrd = uInstr[13]; MDRwr = uInstr[14]; IRwr = uInstr[15];
  //   FLGwr = uInstr[16]; MEMsel[1:0] = uInstr[18:17]; MEMwr = uInstr[19]; MEMrd = uInstr[20]
endmodule

module Q9_Controler (
  input  [7:0] Opcode,
  input  clk,
  input  rst,
  input  [3:0] Flags,
  output [20:0] uInstr
);

  wire Exec, multiplexer_1_out, xor_1_out;
  wire [1:0] uJump;
  wire [3:0] Action;
  wire [7:0] adder_1_out, multiplexer_2_out, Translate_out, uAddr_q;
  wire [24:4] rom_1_data;

  PLA #(.in_width(8), .out_width(8), .\table ("00000000 00000010 # NOP")) Translate (.in(Opcode), .out(Translate_out));
  Multiplexer #(.select(2)) multiplexer_1 (
    .in0(Flags[0]), .in1(Flags[1]), .in2(Flags[2]), .in3(Flags[3]), .out(multiplexer_1_out), .sel(Action[1:0]));
  Multiplexer #(.select(2), .width(8)) multiplexer_2 (
    .in0({8{1'b0}}), .in1(adder_1_out), .in2(Translate_out), .out(multiplexer_2_out), .sel(uJump));  // open: in3
  xor xor_1 (xor_1_out, multiplexer_1_out, Action[2]);
  Register #(.trigger("falling")) uAddr (.D(multiplexer_2_out), .en(1'b1), .clk(clk), .Q(uAddr_q), .clr(rst));
  or or_1 (Exec, xor_1_out, Action[3]);
  Multiplexer #(.width(2)) multiplexer_3 (.in0(2'b01), .in1(Action[1:0]), .out(uJump), .sel(Action[3]));
  Adder adder_1 (.a(8'h1), .b(uAddr_q), .out(adder_1_out));  // open: cin, cout
  ROM #(.dataWidth(25)) rom_1 (.addr(uAddr_q), .data({rom_1_data, Action}));
  assign uInstr = Exec ? rom_1_data : 21'bz;  // Controlled_Buffer controlled_buffer_1
  Pull_Resistor pull_resistor_1 (.node(uInstr));

  // Notes on the sheet:
  //   contents of rom_1 (hex, n*v repeats v):
  //   3ff81 2a 4
  //   0000  CondN
  //   0001  CondZ
  //   0010  CondC
  //   0010  CondSC
  //   0100  CondNN
  //   0101  CondNZ
  //   0110  CondNC
  //   0010  CondNSC
  //   1000  FETCH
  //   1001  NEXT
  //   1010  DISPATCH
endmodule
